// Digital circuit AC.dig as structural Verilog
module AC (
  input  [7:0] D_In,
  input  C_AC,
  input  W_En,
  output [7:0] D_Out
);

  wire multiplexer_1_out, multiplexer_2_out, multiplexer_3_out, multiplexer_4_out, multiplexer_5_out,
       multiplexer_6_out, multiplexer_7_out, multiplexer_8_out;

  Multiplexer multiplexer_1 (.sel(W_En), .in_0(D_Out[0]), .in_1(D_In[0]), .out(multiplexer_1_out));
  Multiplexer multiplexer_2 (.sel(W_En), .in_0(D_Out[1]), .in_1(D_In[1]), .out(multiplexer_2_out));
  Multiplexer multiplexer_3 (.sel(W_En), .in_0(D_Out[2]), .in_1(D_In[2]), .out(multiplexer_3_out));
  Multiplexer multiplexer_4 (.sel(W_En), .in_0(D_Out[3]), .in_1(D_In[3]), .out(multiplexer_4_out));
  Multiplexer multiplexer_5 (.sel(W_En), .in_0(D_Out[4]), .in_1(D_In[4]), .out(multiplexer_5_out));
  Multiplexer multiplexer_6 (.sel(W_En), .in_0(D_Out[5]), .in_1(D_In[5]), .out(multiplexer_6_out));
  Multiplexer multiplexer_7 (.sel(W_En), .in_0(D_Out[6]), .in_1(D_In[6]), .out(multiplexer_7_out));
  Multiplexer multiplexer_8 (.sel(W_En), .in_0(D_Out[7]), .in_1(D_In[7]), .out(multiplexer_8_out));
  D_FF d_ff_1 (.D(multiplexer_1_out), .C(C_AC), .Q(D_Out[0]));  // open: nQ
  D_FF d_ff_2 (.D(multiplexer_2_out), .C(C_AC), .Q(D_Out[1]));  // open: nQ
  D_FF d_ff_3 (.D(multiplexer_3_out), .C(C_AC), .Q(D_Out[2]));  // open: nQ
  D_FF d_ff_4 (.D(multiplexer_4_out), .C(C_AC), .Q(D_Out[3]));  // open: nQ
  D_FF d_ff_5 (.D(multiplexer_5_out), .C(C_AC), .Q(D_Out[4]));  // open: nQ
  D_FF d_ff_6 (.D(multiplexer_6_out), .C(C_AC), .Q(D_Out[5]));  // open: nQ
  D_FF d_ff_7 (.D(multiplexer_7_out), .C(C_AC), .Q(D_Out[6]));  // open: nQ
  D_FF d_ff_8 (.D(multiplexer_8_out), .C(C_AC), .Q(D_Out[7]));  // open: nQ

  // Other names for the same wires on the sheet: CLK_AC = C_AC; Di0 = D_In[0]; Di1 = D_In[1]; Di2 = D_In[2];
  //   Di3 = D_In[3]; Di4 = D_In[4]; Di5 = D_In[5]; Di6 = D_In[6]; Di7 = D_In[7]; Do0 = D_Out[0]; Do1 = D_Out[1];
  //   Do2 = D_Out[2]; Do3 = D_Out[3]; Do4 = D_Out[4]; Do5 = D_Out[5]; Do6 = D_Out[6]; Do7 = D_Out[7]
endmodule
