// Digital circuit CPU.dig as structural Verilog
module CPU (
  input  CLK,
  output [7:0] S
);

  wire decoder_1_out_0, decoder_1_out_1, decoder_1_out_2, decoder_1_out_3, decoder_1_out_4, decoder_1_out_5,
       decoder_1_out_6, decoder_1_out_7, or_1_out, Q, Q_t, UC;
  wire [2:0] op;
  wire [7:0] Ad_Out, D_AC, D_RAM;

  PC pc_1 (.C_PC(Q_t), .EN_PC(Q_t), .Ad_Out(Ad_Out));  // open: S
  AC ac_1 (.D_In(S), .C_AC(CLK), .W_En(UC), .D_Out(D_AC));
  D_FF d_ff_1 (.D(Q_t), .C(CLK), .Q(Q), .nQ(Q_t));
  RAMDualPort #(.AddrBits(8), .Bits(8)) ramdualport_1 (
    .A(Ad_Out), .Din(D_AC), .str(1'b0), .C(CLK), .ld(1'b1), .D(D_RAM));
  Decoder #(.Selector_Bits(3)) decoder_1 (
    .sel(op), .out_0(decoder_1_out_0), .out_1(decoder_1_out_1), .out_2(decoder_1_out_2),
    .out_3(decoder_1_out_3), .out_4(decoder_1_out_4), .out_5(decoder_1_out_5), .out_6(decoder_1_out_6),
    .out_7(decoder_1_out_7));
  or or_1 (or_1_out, decoder_1_out_0, decoder_1_out_1, decoder_1_out_2, decoder_1_out_3, decoder_1_out_4, decoder_1_out_5, decoder_1_out_6, decoder_1_out_7);
  IR ir_1 (.D(D_RAM), .C_IR(Q_t), .op(op));  // open: Q
  alu_cpu alu_cpu_1 (.A(D_AC), .Op(op), .B(D_RAM), .S(S));
  and and_1 (UC, or_1_out, Q);
endmodule
