// Digital circuit IR.dig as structural Verilog
module IR (
  input  [7:0] D,
  input  C_IR,
  output [7:0] Q,
  output [2:0] op
);

  D_FF d_ff_1 (.D(D[0]), .C(C_IR), .Q(op[0]));  // open: nQ
  D_FF d_ff_2 (.D(D[1]), .C(C_IR), .Q(op[1]));  // open: nQ
  D_FF d_ff_3 (.D(D[2]), .C(C_IR), .Q(op[2]));  // open: nQ
  D_FF d_ff_4 (.D(D[3]), .C(C_IR), .Q(Q[3]));  // open: nQ
  D_FF d_ff_5 (.D(D[4]), .C(C_IR), .Q(Q[4]));  // open: nQ
  D_FF d_ff_6 (.D(D[5]), .C(C_IR), .Q(Q[5]));  // open: nQ
  D_FF d_ff_7 (.D(D[6]), .C(C_IR), .Q(Q[6]));  // open: nQ
  D_FF d_ff_8 (.D(D[7]), .C(C_IR), .Q(Q[7]));  // open: nQ

  assign Q[2:0] = op;

  // Other names for the same wires on the sheet: CLK = C_IR; Q0 = op[0]; Q1 = op[1]; Q2 = op[2]
endmodule
