// Digital circuit PC.dig as structural Verilog
module PC (
  input  C_PC,
  input  EN_PC,
  output [7:0] Ad_Out,
  output [7:0] S
);

  Register #(.Bits(8)) register_1 (.D(S), .C(C_PC), .en(EN_PC), .Q(Ad_Out));
  // soma_8bit soma_8bit_1: pin names not known; wires that end beside it: Ad_Out, 8'h1, S[3:0], S[7:4]

  // Other names for the same wires on the sheet: Address_Out[7:0] = Ad_Out
endmodule
