// Digital circuit alu_cpu.dig as structural Verilog
module alu_cpu (
  input  [7:0] A,
  input  [2:0] Op,
  input  [7:0] B,
  output [7:0] S
);

  wire soma_8bit_1_p4, subtracao_8bit_1_p5;
  wire [7:0] divisor_ac, divisor_mq, multiplicador_ac, multiplicador_mq, shift_left, shift_right, soma,
       subtracao;

  // soma_8bit soma_8bit_1: pin names not known; wires that end beside it: A, B, soma[3:0], soma_8bit_1_p4, soma[7:4]
  // subtracao_8bit subtracao_8bit_1: pin names not known; wires that end beside it: A, B, 1'b1, subtracao[3:0], subtracao_8bit_1_p5, subtracao[7:4]
  // multiplicacao_8bit multiplicacao_8bit_1: pin names not known; wires that end beside it: A, B, multiplicador_ac, multiplicador_mq
  // divisor_8bit divisor_8bit_1: pin names not known; wires that end beside it: A, B, divisor_mq, divisor_ac
  // shift_left shift_left_1: pin names not known; wires that end beside it: A, shift_left
  // shift_right shift_right_1: pin names not known; wires that end beside it: A, shift_right
  LED led_1 (.in(subtracao_8bit_1_p5));
  LED led_2 (.in(soma_8bit_1_p4));
  Multiplexer #(.Selector_Bits(3), .Bits(8)) multiplexer_1 (
    .sel(Op), .in_0(soma), .in_1(subtracao), .in_2(multiplicador_ac), .in_3(multiplicador_mq),
    .in_4(divisor_mq), .in_5(divisor_ac), .in_6(shift_left), .in_7(shift_right), .out(S));
endmodule
